# Fritzing sketch POE_Final_Circuit (saved by Fritzing 0.9.2b)
breadboards: 2

parts:
  U2 = 74HC595 [package="DIP16 [THT]"]
  U4 = 74HC595 [package="DIP16 [THT]"]
  U3 = 74HC595 [package="DIP16 [THT]"]
  IC1 = ULN2803A [package=THT]
  U5 = 74HC595 [package="DIP16 [THT]"]
  IC2 = ULN2803A [package=THT]
  IC3 = ULN2803A [package=THT]
  IC4 = ULN2803A [package=THT]
  Part1 = Arduino Uno (Rev3)
  VALVE1 = Plastic Solenoid Valve
  12V_Power = Power plug
  1n4007 = Diode [package=diode-1n4001]
  PSMN022-30PL = Basic FET N-Channel [package="TO220 [THT]"]
  R1 = Resistor [tolerance=±5% resistance=10k package=THT]

nets:
  N1: U2.Q1, IC3.In_2
  N2: U2.Q2, IC3.In_3
  N3: U2.Q3, IC3.In_4
  N4: U2.Q4, IC3.In_5
  N5: U2.Q5, IC3.In_6
  N6: U2.Q6, IC3.In_7
  N7: U2.Q7, IC3.In_8
  GND: U2.GND, U2.OE, U4.GND, U4.OE, U3.GND, U3.OE, IC1.0V, U5.GND, U5.OE, IC2.0V, IC3.0V, IC4.0V, Part1.GND, 12V_Power.GND, PSMN022-30PL.source
  N8: U2.Q7', U3.DS
  VCC: U2.MR, U2.VCC, U4.MR, U4.VCC, U3.MR, U3.VCC, IC1.COM_-_Common, U5.MR, U5.VCC, IC2.COM_-_Common, IC3.COM_-_Common, IC4.COM_-_Common, Part1.5V, R1.Pin_1
  N9: U2.SH_CP, U4.SH_CP, U3.SH_CP, U5.SH_CP, Part1.D12/MISO
  N10: U2.ST_CP, U4.ST_CP, U3.ST_CP, U5.ST_CP, Part1.D8
  N11: U2.DS, U5.Q7'
  N12: U2.Q0, IC3.In_1
  N13: U4.Q1, IC4.In_2
  N14: U4.Q2, IC4.In_3
  N15: U4.Q3, IC4.In_4
  N16: U4.Q4, IC4.In_5
  N17: U4.Q5, IC4.In_6
  N18: U4.Q6, IC4.In_7
  N19: U4.Q7, IC4.In_8
  N20: U4.DS, U3.Q7'
  N21: U4.Q0, IC4.In_1
  N22: U3.Q1, IC1.In_2
  N23: U3.Q2, IC1.In_3
  N24: U3.Q3, IC1.In_4
  N25: U3.Q4, IC1.In_5
  N26: U3.Q5, IC1.In_6
  N27: U3.Q6, IC1.In_7
  N28: U3.Q7, IC1.In_8
  N29: U3.Q0, IC1.In_1
  N30: U5.Q1, IC2.In_2
  N31: U5.Q2, IC2.In_3
  N32: U5.Q3, IC2.In_4
  N33: U5.Q4, IC2.In_5
  N34: U5.Q5, IC2.In_6
  N35: U5.Q6, IC2.In_7
  N36: U5.Q7, IC2.In_8
  N37: U5.DS, Part1.D11_PWM/MOSI
  N38: U5.Q0, IC2.In_1
  N39: IC4.Out_1, PSMN022-30PL.gate, R1.Pin_0
  N40: VALVE1.no_name_yet#1, 12V_Power.VCC, 1n4007.C
  N41: VALVE1.no_name_yet#2, 1n4007.A, PSMN022-30PL.drain
